# Fritzing sketch Rube-Goldberg (saved by Fritzing 0.9.3b)
breadboards: 1

parts:
  L031K6 = STM32F40x [package="LQFP64, 10x10mm"]
  Photocell = PHOTOCELL [package=photocell]
  R1 = Resistor [tolerance=±5% resistance=1k package="2512 [SMD]"]
  Microphone = MIC [package=mic_electret_smd]
  LED1 = LEDs [package=led10mm]
  Marble_Switch = SWITCH-MOMENTARY-2 [package=tactile_switch_tall]
  Marble_Motor = DC Motor
  R2 = Resistor [tolerance=±5% resistance=100 package="2512 [SMD]"]
  Speaker = Loudspeaker
  Motor_Driver = Basic FET P-Channel [package="DPak [SMD]"]
  VCC1 = Battery block 9V
  R3 = Resistor [tolerance=±5% resistance=100k package="2512 [SMD]"]
  R4 = Resistor [tolerance=±5% resistance=100 package="2512 [SMD]"]
  Flyback = Rectifier Diode [part_number=1N4001 package="300 mil [THT]"]

nets:
  N1: L031K6.VBAT, Photocell.P$1, Marble_Switch.2
  GND: L031K6.PA1, L031K6.PA12, Photocell.P$2, R1.Pin_0, Microphone.1, LED1.C, Marble_Switch.1, Speaker.pin2, Motor_Driver.source, VCC1.-, R3.Pin_0
  N2: L031K6.PB0, R2.Pin_0
  N3: L031K6.PA8, R1.Pin_1, Microphone.2
  N4: L031K6.PB3, Motor_Driver.Gate, R3.Pin_1
  N5: L031K6.PB5, R4.Pin_1
  N6: LED1.A, R4.Pin_0
  N7: Marble_Motor.pin_1, VCC1.+, Flyback.cathode
  N8: Marble_Motor.pin_2, Motor_Driver.drain, Flyback.anode
  N9: R2.Pin_1, Speaker.pin1
